// Logisim project B98729 - ALU.circ as structural Verilog: 2 circuits, main circuit main
module main (
  input  Cin,
  input  Bin,
  input  [31:0] A,
  input  [31:0] B,
  input  [3:0] Opcode,
  output Cout,
  output Negative,
  output Zero_Flag,
  output [31:0] Y
);

  wire comparator_1_lt;
  wire [4:0] bitselector_1_out;
  wire [6:0] bitadder_1_out;
  wire [31:0] adder_1_out_4, and_1_out, bit_extender_1_out, bit_extender_2_out, divider_1_out, divider_1_rem,
       multiplier_1_out, nand_1_out, or_1_out, shifter_1_out, shifter_2_out, shifter_3_out, shifter_4_out,
       subtractor_1_out, xnor_1_out, xor_1_out;

  BitSelector #(.width(32), .group(5)) bitselector_1 (.in(B), .out(bitselector_1_out), .sel(3'b000));
  Adder adder_1 (.in_2(A), .in_3(B), .Cin(Cin), .out_4(adder_1_out_4), .Overflow(Cout));
  assign and_1_out = A & B;  // AND_Gate and_1, 32 bits wide
  assign or_1_out = A | B;  // OR_Gate or_1, 32 bits wide
  assign xor_1_out = A ^ B;  // XOR_Gate xor_1, 32 bits wide
  Shifter #(.width(32), .shift("lr")) shifter_1 (.in(A), .\dist (bitselector_1_out), .out(shifter_1_out));
  Shifter #(.width(32), .shift("ar")) shifter_2 (.in(A), .\dist (bitselector_1_out), .out(shifter_2_out));
  Shifter #(.width(32)) shifter_3 (.in(A), .\dist (bitselector_1_out), .out(shifter_3_out));
  Shifter #(.width(32)) shifter_4 (.in(A), .\dist (bitselector_1_out), .out(shifter_4_out));
  Comparator #(.width(32)) comparator_1 (.a(A), .b(B), .lt(comparator_1_lt));  // open: gt, eq
  Divider #(.width(32)) divider_1 (.a(A), .b(B), .out(divider_1_out), .rem(divider_1_rem));  // open: upper
  Multiplier #(.width(32)) multiplier_1 (.a(A), .b(B), .out(multiplier_1_out));  // open: cin, cout
  Subtractor #(.width(32)) subtractor_1 (.a(A), .b(B), .out(subtractor_1_out), .bin(Bin), .bout(Negative));
  BitAdder #(.width(32)) bitadder_1 (.in0(A), .in1(B), .out(bitadder_1_out));
  assign nand_1_out = ~(A & B);  // NAND_Gate nand_1, 32 bits wide
  assign bit_extender_1_out = {{31{1'b0}}, comparator_1_lt};  // Bit_Extender bit_extender_1
  assign bit_extender_2_out = {{25{1'b0}}, bitadder_1_out};  // Bit_Extender bit_extender_2
  assign xnor_1_out = ~(A ^ B);  // XNOR_Gate xnor_1, 32 bits wide
  Multiplexer #(.select(4), .width(32), .enable("false")) multiplexer_1 (
    .in0(adder_1_out_4), .in1(and_1_out), .in2(or_1_out), .in3(xor_1_out), .in4(shifter_1_out),
    .in5(shifter_2_out), .in6(shifter_3_out), .in7(shifter_4_out), .in8(bit_extender_1_out),
    .in9(divider_1_out), .in10(divider_1_rem), .in11(multiplier_1_out), .in12(subtractor_1_out),
    .in13(bit_extender_2_out), .in14(nand_1_out), .in15(xnor_1_out), .out(Y), .sel(Opcode));
  Comparator #(.width(32)) comparator_2 (.a(Y), .b({32{1'b0}}), .eq(Zero_Flag));  // open: gt, lt

  // Notes on the sheet:
  //   Entradas:
  //   A: Operando de 32 bits
  //   B: Operando de 32 bits
  //   Cin: Bit de acarreo
  //   Bin: Bit de borrow para resta
  //   Opcode: Código de operación
  //   ALU - B98729
  //   Salidas:
  //   Y: Resultado de la operación
  //   Negative: Si el resultado de la resta es negativo
  //   Zero: Bandera que determina si el resultado es cero
  //   Cout: Bandera que determina si hubo overflow 
endmodule

module Adder (
  input  Cin,
  input  [31:0] in_2,
  input  [31:0] in_3,
  output [31:0] out_4,
  output Overflow
);

  wire adder_1_cout, adder_2_cout;

  Adder_part #(.width(31)) adder_1 (.a(in_2[30:0]), .b(in_3[30:0]), .out(out_4[30:0]), .cin(Cin), .cout(adder_1_cout));
  Adder_part #(.width(1)) adder_2 (
    .a(in_2[31]), .b(in_3[31]), .out(out_4[31]), .cin(adder_1_cout), .cout(adder_2_cout));
  xor xor_1 (Overflow, adder_1_cout, adder_2_cout);

  // Notes on the sheet:
  //   ALU - B98729
endmodule
